// Logisim project 2input7.circ as structural Verilog: 3 circuits, main circuit main
module main (
  input  A,
  input  B
);

  wire and_1_out, not_1_out, not_2_out, or_1_out, or_2_out;

  not not_1 (not_1_out, A);
  not not_2 (not_2_out, B);
  or or_1 (or_1_out, not_2_out, A);
  or or_2 (or_2_out, not_1_out, B);
  and and_1 (and_1_out, not_2_out, not_1_out);
  _7_Segment_Display u_7_segment_display_1 (
    .g(A), .f(and_1_out), .a(or_1_out), .b(1'b1), .e(not_2_out), .d(or_1_out), .c(or_2_out));  // open: dp
endmodule

module simp (
  input  A,
  input  B
);

  wire a_d_out, c_e_out, f_out, not_1_out, not_2_out;

  not not_1 (not_1_out, A);
  not not_2 (not_2_out, B);
  nand a_d (a_d_out, B, not_1_out);
  nand c_e (c_e_out, A, not_2_out);
  nor f (f_out, B, A);
  _7_Segment_Display u_7_segment_display_1 (
    .g(A), .f(f_out), .a(a_d_out), .b(1'b1), .e(not_2_out), .d(a_d_out), .c(c_e_out));  // open: dp
  // NOR_Gate nor_1 is placed but not wired
endmodule

module xx (
  input  a,
  input  b
);

  wire inv_pin6, inv_pin8, inv_pin12, n7402_1_p2, nord_pin3, nord_pin11;

  _7404 inv (
    .pin6(inv_pin6), .pin13(a), .pin12(inv_pin12), .pin9(b), .pin8(inv_pin8));  // open: pin1, pin2, pin3, pin4, pin5, pin11, pin10
  _7400 nord (
    .pin1(inv_pin8), .pin2(a), .pin3(nord_pin3), .pin13(inv_pin12), .pin12(b), .pin11(nord_pin11));  // open: pin4, pin5, pin6, pin10, pin9, pin8
  // _7402 7402_1: pin names not known; wires that end beside it: 1'b1, n7402_1_p2, a, b, 1'b0
  _7_Segment_Display u_7_segment_display_1 (
    .g(a), .f(n7402_1_p2), .a(nord_pin11), .b(1'b1), .e(inv_pin8), .d(nord_pin11), .c(nord_pin3));  // open: dp
  // also tied to GND on the sheet: inv_pin6
endmodule
