// Logisim project 4input7.circ as structural Verilog: 3 circuits, main circuit main
module main (
  input  w,
  input  x,
  input  y,
  input  z
);

  wire not_1_out, not_2_out, not_3_out, not_4_out, notwnotxnoty_out, notwnotxnotyz_out, notwnotxz_out,
       notxy_out, notxynotz_out, or_1_out, or_2_out, or_3_out, or_4_out, or_5_out, or_6_out, xnoty_out,
       xnotynotz_out, xnotyz_out, xynotz_out, xyz_out, yz_out;

  not not_1 (not_1_out, w);
  not not_2 (not_2_out, x);
  not not_3 (not_3_out, y);
  not not_4 (not_4_out, z);
  and notwnotxnotyz (notwnotxnotyz_out, not_1_out, not_2_out, not_3_out, z);
  and xnotynotz (xnotynotz_out, x, not_3_out, not_4_out);
  and xnotyz (xnotyz_out, x, not_3_out, z);
  and xynotz (xynotz_out, x, y, not_4_out);
  and notxynotz (notxynotz_out, not_2_out, y, not_4_out);
  and xyz (xyz_out, x, y, z);
  and xnoty (xnoty_out, x, not_3_out);
  and notwnotxz (notwnotxz_out, not_1_out, not_2_out, z);
  and yz (yz_out, y, z);
  and notxy (notxy_out, not_2_out, y);
  and notwnotxnoty (notwnotxnoty_out, not_1_out, not_2_out, not_3_out);
  or or_1 (or_1_out, notwnotxnotyz_out, xnotynotz_out);
  or or_2 (or_2_out, xnotyz_out, xynotz_out);
  or or_3 (or_3_out, notwnotxnotyz_out, xyz_out, xnotynotz_out);
  or or_4 (or_4_out, z, xnoty_out);
  or or_5 (or_5_out, notwnotxz_out, yz_out, notxy_out);
  or or_6 (or_6_out, notwnotxnoty_out, xyz_out);
  _7_Segment_Display #(.active("false")) u_7_segment_display_1 (
    .g(or_6_out), .f(or_5_out), .a(or_1_out), .b(or_2_out), .e(or_4_out), .d(or_3_out), .c(notxynotz_out),
    .dp(1'b1));
endmodule

module demorgan (
  input  w,
  input  x,
  input  y,
  input  z
);

  wire nand_1_out, nand_2_out, nand_3_out, nand_4_out, nand_5_out, nand_6_out, nand_7_out, nand_8_out,
       nand_9_out, nand_10_out, nand_11_out, nand_12_out, nand_13_out, nand_14_out, nand_15_out, nand_16_out,
       nor_1_out, not_1_out, not_2_out, not_3_out, not_4_out;

  not not_1 (not_1_out, w);
  not not_2 (not_2_out, x);
  not not_3 (not_3_out, y);
  not not_4 (not_4_out, z);
  nand nand_1 (nand_1_out, not_1_out, not_2_out, not_3_out, z);
  nand nand_2 (nand_2_out, x, not_3_out, not_4_out);
  nand nand_3 (nand_3_out, x, not_3_out, z);
  nand nand_4 (nand_4_out, x, y, not_4_out);
  nor nor_1 (nor_1_out, x, not_3_out, z);
  nand nand_5 (nand_5_out, x, y, z);
  nand nand_6 (nand_6_out, x, not_3_out);
  nand nand_7 (nand_7_out, not_1_out, not_2_out, z);
  nand nand_8 (nand_8_out, y, z);
  nand nand_9 (nand_9_out, not_2_out, y);
  nand nand_10 (nand_10_out, not_1_out, not_2_out, not_3_out);
  nand nand_11 (nand_11_out, nand_1_out, nand_2_out);
  nand nand_12 (nand_12_out, nand_3_out, nand_4_out);
  nand nand_13 (nand_13_out, nand_1_out, nand_5_out, nand_2_out);
  nand nand_14 (nand_14_out, not_4_out, nand_6_out);
  nand nand_15 (nand_15_out, nand_7_out, nand_8_out, nand_9_out);
  nand nand_16 (nand_16_out, nand_10_out, nand_5_out);
  _7_Segment_Display #(.active("false")) u_7_segment_display_1 (
    .g(nand_16_out), .f(nand_15_out), .a(nand_11_out), .b(nand_12_out), .e(nand_14_out), .d(nand_13_out),
    .c(nor_1_out), .dp(1'b1));

  // Notes on the sheet:
  //   98 transistors
endmodule

module demorgna2minus (
  input  w,
  input  x,
  input  y,
  input  z
);

  wire nand_1_out, nand_2_out, nand_3_out, nand_4_out, nand_5_out, nand_6_out, nand_7_out, nand_8_out,
       nand_9_out, nand_10_out, nand_11_out, nand_12_out, nand_13_out, nand_14_out, nor_1_out, not_1_out,
       not_2_out, not_3_out, not_4_out, xxx_out, xxxx_out;

  not not_1 (not_1_out, w);
  not not_2 (not_2_out, x);
  not not_3 (not_3_out, y);
  not not_4 (not_4_out, z);
  nand nand_1 (nand_1_out, not_1_out, not_2_out, not_3_out, z);
  nand nand_2 (nand_2_out, x, not_3_out, not_4_out);
  nand nand_3 (nand_3_out, x, not_3_out, z);
  nand nand_4 (nand_4_out, x, y, not_4_out);
  nor nor_1 (nor_1_out, x, not_3_out, z);
  nand nand_5 (nand_5_out, x, y, z);
  nand xxx (xxx_out, x, not_3_out);
  nand xxxx (xxxx_out, not_1_out, not_2_out, z);
  nand nand_6 (nand_6_out, y, z);
  nand nand_7 (nand_7_out, not_2_out, y);
  nand nand_8 (nand_8_out, not_1_out, not_2_out, not_3_out);
  nand nand_9 (nand_9_out, nand_1_out, nand_2_out);
  nand nand_10 (nand_10_out, nand_3_out, nand_4_out);
  nand nand_11 (nand_11_out, nand_1_out, nand_5_out, nand_2_out);
  nand nand_12 (nand_12_out, not_4_out, nand_2_out);
  nand nand_13 (nand_13_out, nand_1_out, nand_6_out, nand_7_out);
  nand nand_14 (nand_14_out, nand_8_out, nand_5_out);
  _7_Segment_Display #(.active("false")) u_7_segment_display_1 (
    .g(nand_14_out), .f(nand_13_out), .a(nand_9_out), .b(nand_10_out), .e(nand_12_out), .d(nand_11_out),
    .c(nor_1_out), .dp(1'b1));

  // Notes on the sheet:
  //   88 transistors
endmodule
