// Logisim project 7table.circ as structural Verilog: 3 circuits, main circuit main
module main (
  input  x,
  input  y,
  input  z,
  output a,
  output b,
  output c,
  output d,
  output e,
  output f,
  output g
);

  wire and_1_out, and_2_out, and_3_out, and_4_out, and_5_out, and_6_out, not_1_out, not_2_out, not_3_out;

  not not_1 (not_1_out, y);
  not not_2 (not_2_out, x);
  not not_3 (not_3_out, z);
  and and_1 (and_1_out, not_2_out, not_1_out, not_3_out);
  and and_2 (and_2_out, not_2_out, not_1_out, z);
  and and_3 (and_3_out, not_2_out, y, not_3_out);
  and and_4 (and_4_out, not_2_out, y, z);
  and and_5 (and_5_out, x, not_1_out, not_3_out);
  and and_6 (and_6_out, x, not_1_out, z);
  or or_1 (a, and_2_out, and_3_out, and_4_out, and_5_out, and_6_out);
  or or_2 (b, and_2_out, and_4_out);
  or or_3 (c, and_2_out, and_3_out, and_4_out, and_6_out);
  or or_4 (e, and_1_out, and_2_out, and_4_out, and_5_out);
  or or_5 (d, and_1_out, and_3_out, and_5_out, and_6_out);
  _7_Segment_Display u_7_segment_display_1 (.g(c), .f(1'b1), .a(a), .b(b), .e(e), .d(d), .c(c));  // open: dp

  assign f = 1'b1;
  assign g = c;
endmodule

module simplified (
  input  x,
  input  y,
  input  z
);

  wire and_1_out, and_2_out, not_1_out, not_2_out, not_3_out, or_1_out, or_2_out, or_3_out, or_4_out,
       or_5_out;

  not not_1 (not_1_out, x);
  not not_2 (not_2_out, y);
  not not_3 (not_3_out, z);
  or or_1 (or_1_out, not_2_out, z);
  or or_2 (or_2_out, not_1_out, not_3_out);
  or or_3 (or_3_out, z, y, x);
  and and_1 (and_1_out, z, not_1_out);
  or or_4 (or_4_out, z, y);
  or or_5 (or_5_out, x, not_3_out);
  and and_2 (and_2_out, or_1_out, or_2_out);
  _7_Segment_Display u_7_segment_display_1 (
    .g(or_4_out), .f(1'b1), .a(or_3_out), .b(and_1_out), .e(and_2_out), .d(or_5_out), .c(or_4_out));  // open: dp

  // Notes on the sheet:
  //   52 Transistors
endmodule

module demorgan (
  input  x,
  input  y,
  input  z
);

  wire nand_1_out, nand_2_out, nand_3_out, nand_4_out, nand_5_out, nand_6_out, nor_1_out, not_1_out,
       not_2_out, not_3_out;

  not not_1 (not_1_out, x);
  not not_2 (not_2_out, y);
  not not_3 (not_3_out, z);
  nand nand_1 (nand_1_out, not_3_out, not_2_out, not_1_out);
  nor nor_1 (nor_1_out, not_3_out, x);
  nand nand_2 (nand_2_out, not_3_out, not_2_out);
  nand nand_3 (nand_3_out, not_2_out, not_3_out);
  nand nand_4 (nand_4_out, not_1_out, z);
  nand nand_5 (nand_5_out, not_1_out, z);
  nand nand_6 (nand_6_out, nand_3_out, nand_4_out);
  _7_Segment_Display u_7_segment_display_1 (
    .g(nand_2_out), .f(1'b1), .a(nand_1_out), .b(nor_1_out), .e(nand_6_out), .d(nand_5_out), .c(nand_2_out));  // open: dp

  // Notes on the sheet:
  //   36 Transistors
endmodule
