// Logisim project CLA.circ as structural Verilog
module CLA_C4_1 (
  input  c0,
  input  G0,
  input  p0,
  input  g1,
  input  p1,
  input  g2,
  input  p2,
  input  g3,
  input  p3,
  output out_10
);

  wire and_1_out, and_2_out, and_3_out, and_4_out;

  and and_1 (and_1_out, G0, p1, p2, p3);
  and and_2 (and_2_out, g1, p2, p3);
  and and_3 (and_3_out, g2, p3);
  and and_4 (and_4_out, c0, p0, p1, p2, p3);
  or or_1 (out_10, and_4_out, and_1_out, and_2_out, and_3_out, g3);
endmodule

module CLA_C4_2 (
  input  g3,
  input  g2,
  input  g1,
  input  g0,
  input  p3,
  input  p2,
  input  p1,
  input  p0,
  input  c,
  output out_10
);

  wire nand_1_out, nand_2_out, nand_3_out, nor_1_out, nor_2_out, nor_3_out, nor_4_out, not_1_out, not_2_out,
       not_3_out, not_4_out, not_5_out;

  not not_1 (not_1_out, p0);
  not not_2 (not_2_out, c);
  nand nand_1 (nand_1_out, p3, p2, p1);
  not not_3 (not_3_out, g0);
  nor nor_1 (nor_1_out, not_1_out, nand_1_out, not_2_out);
  nand nand_2 (nand_2_out, g2, p3);
  not not_4 (not_4_out, nand_2_out);
  nand nand_3 (nand_3_out, p3, g1, p2);
  not not_5 (not_5_out, nand_3_out);
  nor nor_2 (nor_2_out, not_3_out, nand_1_out);
  nor nor_3 (nor_3_out, g3, not_4_out, not_5_out);
  nor nor_4 (nor_4_out, nor_2_out, nor_1_out);
  nand nand_4 (out_10, nor_3_out, nor_4_out);
endmodule

module AOI21 (
  input  c,
  input  b,
  input  a,
  output out_4
);

  wire transistor_1_out, transistor_3_out;

  Transistor transistor_1 (.in(1'b1), .out(transistor_1_out), .gate(c));
  Transistor #(.\type ("n")) transistor_2 (.in(transistor_3_out), .out(out_4), .gate(c));
  Transistor #(.\type ("n")) transistor_3 (.in(1'b0), .out(transistor_3_out), .gate(b));
  Transistor transistor_4 (.in(transistor_1_out), .out(out_4), .gate(a));
  Transistor transistor_5 (.in(1'b1), .out(transistor_1_out), .gate(b));
  Transistor #(.\type ("n")) transistor_6 (.in(1'b0), .out(out_4), .gate(a));
endmodule

module CLA_C4_3 (
  input  c,
  input  p0,
  input  p1,
  input  p2,
  input  p3,
  input  g0,
  input  g1,
  input  g2,
  input  g3,
  input  in_10,
  input  in_11,
  input  in_12,
  input  in_13,
  input  in_14,
  input  in_15,
  input  in_16,
  input  in_17,
  input  in_18,
  output out_19,
  output out_20
);

  wire aoi21_1_out_4, aoi21_2_out_4, nand_1_out, nand_2_out, nand_3_out, nand_4_out, nand_5_out, nand_6_out,
       nand_7_out, nor_1_out, nor_2_out, nor_3_out, nor_4_out, nor_5_out, nor_6_out, not_1_out, not_2_out,
       not_3_out, not_4_out, not_5_out, not_6_out, not_7_out, not_8_out;

  not not_1 (not_1_out, g0);
  not not_2 (not_2_out, p0);
  nand nand_1 (nand_1_out, p2, g1, p3);
  not not_3 (not_3_out, in_17);
  nand nand_2 (nand_2_out, p1, p2, p3);
  not not_4 (not_4_out, nand_1_out);
  nand nand_3 (nand_3_out, not_1_out, g2);
  not not_5 (not_5_out, nand_3_out);
  nor nor_1 (nor_1_out, not_2_out, nand_2_out);
  nor nor_2 (nor_2_out, nand_2_out, not_1_out);
  nor nor_3 (nor_3_out, not_4_out, not_5_out);
  nand nand_4 (nand_4_out, in_14, in_15, in_16);
  nor nor_4 (nor_4_out, nor_2_out, g3);
  nand nand_5 (nand_5_out, in_11, in_14);
  not not_6 (not_6_out, nand_5_out);
  nand nand_6 (nand_6_out, in_14, in_12, in_15);
  not not_7 (not_7_out, nand_6_out);
  nand nand_7 (nand_7_out, nor_4_out, nor_3_out);
  nor nor_5 (nor_5_out, in_13, not_3_out, nand_4_out);
  nor nor_6 (nor_6_out, in_10, not_6_out, not_7_out);
  not not_8 (not_8_out, nor_6_out);
  AOI21 aoi21_1 (.c(in_18), .b(nor_5_out), .a(not_8_out), .out_4(aoi21_1_out_4));
  AOI21 aoi21_2 (.c(c), .b(nor_1_out), .a(nand_7_out), .out_4(aoi21_2_out_4));
  not not_9 (out_20, aoi21_1_out_4);
  not not_10 (out_19, aoi21_2_out_4);
endmodule
