// Logisim project xOR.circ as structural Verilog: 2 circuits, main circuit main
module main (
  input  in_1,
  input  in_2,
  output out_3
);

  wire and_1_out, and_2_out, nor_1_out, not_1_out, not_2_out;

  not not_1 (not_1_out, in_2);
  not not_2 (not_2_out, in_1);
  and and_1 (and_1_out, in_1, not_1_out);
  and and_2 (and_2_out, not_2_out, in_2);
  nor nor_1 (nor_1_out, and_1_out, and_2_out);
  not not_3 (out_3, nor_1_out);
endmodule

module myXOR (
  input  a,
  input  b,
  input  c,
  output y
);

  wire main_1_out_3;

  main main_1 (.in_1(a), .in_2(b), .out_3(main_1_out_3));
  main main_2 (.in_1(main_1_out_3), .in_2(c), .out_3(y));
endmodule
